# Fritzing sketch HC12_Transmitter (saved by Fritzing 0.9.3b)
circuit board: 8cm x 5.6cm

parts:
  J1 = female pin header, 5 pins [form="♀ (female)"]
  U2 = Thumb Joystick [package=joystick]
  IC1 = Voltage Regulator [package=to-220-alt]
  Arduino = Arduino Pro Mini (5V) [part_number=Arduino]
  Input = female pin header, 2 pins [form="♀ (female)"]
  J2 = female pin header, 4 pins [form="♀ (female)"]
  U1 = Thumb Joystick [package=joystick]

nets:
  N1: J1.pin1, U2.V+, U2.H-, IC1.OUT, J2.pin2, U1.V+, U1.H-
  GND: J1.pin2, U2.SEL+, U2.H+, U2.V-, IC1.GND, Arduino.GND, Input.pin1, J2.pin1, U1.H+, U1.SEL-, U1.V-
  N2: J1.pin3, Arduino.D2
  N3: J1.pin4, Arduino.D3
  N4: J1.pin5, Arduino.D4
  N5: U2.SEL-, Arduino.D5
  N6: U2.V, Arduino.A1
  N7: U2.H, Arduino.A0
  N8: IC1.IN, Arduino.VCC, Input.pin2
  N9: Arduino.A4, J2.pin4
  N10: Arduino.A5, J2.pin3
  N11: Arduino.A3, U1.V
  N12: Arduino.A2, U1.H
  N13: Arduino.D6, U1.SEL+

notes:
  Oled
  Arduino
  J2
  J1
  +
  -
  7805
  HC12
  RUPAK
  Rupak
  Transmitter
